# Fritzing sketch arduino-ble-board-sketch (saved by Fritzing 0.8.4b)
breadboards: 1

parts:
  R1 = Rotary Potentiometer (Small) [maximum_resistance=10kΩ package=THT]
  Arduino2 = Arduino Uno (Rev3)
  LED2 = smd LED [color="Red (633nm)" package="0603 [SMD]"]
  R2 = Resistor [tolerance=±5% resistance=220 package=THT]

nets:
  N1: R1.leg1, Arduino2.5V
  N2: R1.wiper, Arduino2.A0
  N3: R1.leg2, Arduino2.GND, R2.Pin_0
  N4: Arduino2.D2, LED2.anode
  N5: LED2.cathode, R2.Pin_1
