# Fritzing sketch arduino-led-wifi-sketch (saved by Fritzing 0.8.7b)
breadboards: 1

parts:
  LED2 = smd LED [color="Red (633nm)" package="0603 [SMD]"]
  R2 = Resistor [tolerance=±5% resistance=220 package=THT]
  Arduino2 = Arduino Uno (Rev3)
  Part1 = Arduino Ethernet Shield (Rev3)  # not connected

nets:
  N1: LED2.cathode, R2.Pin_1
  N2: LED2.anode, Arduino2.D2
  N3: R2.Pin_0, Arduino2.GND
